// Logisim project sap1_1.circ as structural Verilog: 1 circuit, main circuit main
module main (
);

  wire A_sw1, A_sw2, A_sw3, A_sw4, and_1_out, button_1_out, CLK, Cp, dipswitch_1_sw1, dipswitch_1_sw2,
       dipswitch_1_sw3, dipswitch_1_sw4, dipswitch_1_sw5, dipswitch_1_sw6, dipswitch_1_sw7, dipswitch_1_sw8,
       Ep, l_74ls107_f74dca52_1_q1, l_74ls107_f74dca52_1_q2, l_74ls107_f74dca52_2_q1,
       l_74ls107_f74dca52_2_q2, l_74ls157_d074910b_1_y1, l_74ls157_d074910b_1_y2, l_74ls157_d074910b_1_y3,
       l_74ls157_d074910b_1_y4, l_74ls173_6bdbcc89_1_g4, l_74ls173_6bdbcc89_1_q1, l_74ls173_6bdbcc89_1_q2,
       l_74ls173_6bdbcc89_1_q3, l_74ls189_c76b68cd_1_not_do1, l_74ls189_c76b68cd_1_not_do2,
       l_74ls189_c76b68cd_1_not_do3, l_74ls189_c76b68cd_1_not_do4, l_74ls189_c76b68cd_2_not_do1,
       l_74ls189_c76b68cd_2_not_do2, l_74ls189_c76b68cd_2_not_do3, l_74ls189_c76b68cd_2_not_do4, NOT_CE,
       NOT_CLK, NOT_CLR, NOT_Lm, RUN_PROG_sw1, S2_sw1;

  DipSwitch dipswitch_1 (
    .sw1(dipswitch_1_sw1), .sw2(dipswitch_1_sw2), .sw3(dipswitch_1_sw3), .sw4(dipswitch_1_sw4),
    .sw5(dipswitch_1_sw5), .sw6(dipswitch_1_sw6), .sw7(dipswitch_1_sw7), .sw8(dipswitch_1_sw8));
  DipSwitch #(.number(1)) RUN_PROG (.sw1(RUN_PROG_sw1));
  DipSwitch #(.number(4)) A (.sw1(A_sw1), .sw2(A_sw2), .sw3(A_sw3), .sw4(A_sw4));
  and and_1 (and_1_out, NOT_CE, RUN_PROG_sw1);
  Button #(.press("passive")) button_1 (.out(button_1_out));
  L_74LS107_f74dca52 l_74ls107_f74dca52_1 (
    .CLK1(NOT_CLK), .K1(Cp), .CLR1(NOT_CLR), .J2(Cp), .CLK2(l_74ls107_f74dca52_1_q1), .K2(Cp),
    .CLR2(NOT_CLR), .J1(Cp), .Q1(l_74ls107_f74dca52_1_q1), .Q2(l_74ls107_f74dca52_1_q2));  // open: NOTQ1, NOTQ2
  L_74LS107_f74dca52 l_74ls107_f74dca52_2 (
    .CLK1(l_74ls107_f74dca52_1_q2), .K1(Cp), .CLR1(NOT_CLR), .J2(Cp), .CLK2(l_74ls107_f74dca52_2_q1),
    .K2(Cp), .CLR2(NOT_CLR), .J1(Cp), .Q1(l_74ls107_f74dca52_2_q1), .Q2(l_74ls107_f74dca52_2_q2));  // open: NOTQ1, NOTQ2
  L_74LS173_6bdbcc89 l_74ls173_6bdbcc89_1 (
    .N(1'b0), .D1(l_74ls189_c76b68cd_1_not_do1), .NOT_G1(NOT_Lm), .NOT_G2(NOT_Lm),
    .D2(l_74ls189_c76b68cd_1_not_do2), .CLK(CLK), .D3(l_74ls189_c76b68cd_1_not_do3),
    .D4(l_74ls189_c76b68cd_1_not_do4), .CLR(1'b0), .M(1'b0), .Q1(l_74ls173_6bdbcc89_1_q1),
    .Q2(l_74ls173_6bdbcc89_1_q2), .Q3(l_74ls173_6bdbcc89_1_q3), .G4(l_74ls173_6bdbcc89_1_g4));
  L_74LS157_d074910b l_74ls157_d074910b_1 (
    .B1(l_74ls173_6bdbcc89_1_g4), .A2(A_sw2), .B2(l_74ls173_6bdbcc89_1_q3), .A3(A_sw3),
    .B3(l_74ls173_6bdbcc89_1_q2), .A4(A_sw4), .B4(l_74ls173_6bdbcc89_1_q1), .STROBE_G(1'b0),
    .SELECT_A_B(S2_sw1), .A1(A_sw1), .Y1(l_74ls157_d074910b_1_y1), .Y2(l_74ls157_d074910b_1_y2),
    .Y3(l_74ls157_d074910b_1_y3), .Y4(l_74ls157_d074910b_1_y4));
  DipSwitch #(.number(1)) S2 (.sw1(S2_sw1));
  L_74LS189_c76b68cd l_74ls189_c76b68cd_1 (
    .A0(l_74ls157_d074910b_1_y4), .A1(l_74ls157_d074910b_1_y3), .A2(l_74ls157_d074910b_1_y2),
    .A3(l_74ls157_d074910b_1_y1), .DI1(dipswitch_1_sw4), .DI2(dipswitch_1_sw3), .DI3(dipswitch_1_sw2),
    .DI4(dipswitch_1_sw1), .NOT_S(and_1_out), .NOT_W(button_1_out), .NOT_DO2(l_74ls189_c76b68cd_1_not_do2),
    .NOT_DO3(l_74ls189_c76b68cd_1_not_do3), .NOT_DO4(l_74ls189_c76b68cd_1_not_do4),
    .NOT_DO1(l_74ls189_c76b68cd_1_not_do1));
  L_74LS189_c76b68cd l_74ls189_c76b68cd_2 (
    .A0(l_74ls157_d074910b_1_y4), .A1(l_74ls157_d074910b_1_y3), .A2(l_74ls157_d074910b_1_y2),
    .A3(l_74ls157_d074910b_1_y1), .DI1(dipswitch_1_sw8), .DI2(dipswitch_1_sw7), .DI3(dipswitch_1_sw6),
    .DI4(dipswitch_1_sw5), .NOT_S(and_1_out), .NOT_W(button_1_out), .NOT_DO2(l_74ls189_c76b68cd_2_not_do2),
    .NOT_DO3(l_74ls189_c76b68cd_2_not_do3), .NOT_DO4(l_74ls189_c76b68cd_2_not_do4),
    .NOT_DO1(l_74ls189_c76b68cd_2_not_do1));
  L_74LS126_5b2bd483 l_74ls126_5b2bd483_1 (
    .A1(l_74ls107_f74dca52_1_q1), .G1(Ep), .A2(l_74ls107_f74dca52_1_q2), .G2(Ep),
    .A3(l_74ls107_f74dca52_2_q1), .G3(Ep), .A4(l_74ls107_f74dca52_2_q2), .G4(Ep),
    .Y1(l_74ls189_c76b68cd_1_not_do4), .Y2(l_74ls189_c76b68cd_1_not_do3), .Y3(l_74ls189_c76b68cd_1_not_do2),
    .Y4(l_74ls189_c76b68cd_1_not_do1));

  // Notes on the sheet:
  //   S2
  //   Program Counter
  //   MAR
  //   2 to 1 Multiplexer
endmodule
